# Fritzing sketch 01.SimpleCircuit (saved by Fritzing 0.9.10b)
circuit board: 8.46667cm x 5.64444cm
breadboards: 1

parts:
  S1 = Pushbutton [package="[THT]"]
  LED1 = LED - 5mm [color="Red (633nm)" current=0.030 package="5 mm [THT]"]
  R1 = Resistor [tolerance=±5% power=0.25 resistance=220 package=THT]
  Teensy1 = Teensy 4.0

nets:
  N1: S1.Pin_1, S1.Pin_2, R1.Pin_0
  N2: S1.Pin_3, S1.Pin_4, Teensy1.pin_31
  N3: LED1.cathode, Teensy1.pin_1, Teensy1.pin_32
  N4: LED1.anode, R1.Pin_1

custom parts:
  Teensy 4.0: The Teensy is a complete USB-based microcontoller development system, in a very small footprint, capable of implementing many types of projects. All programming is done via the USB port. No special programmer is needed, only a standard micro-USB cable and a PC or Macintosh with a USB port.
