# Fritzing sketch 02.FSR (saved by Fritzing 0.9.10b)
breadboards: 1

parts:
  J1 = Basic Force Sensing Resistor (FSR) [package=THT]
  R1 = Resistor [tolerance=±5% power=0.25 resistance=3300 package=THT]
  Teensy1 = Teensy 4.0
  P2 = Multimeter straight black probe
  P1 = Multimeter straight red probe

nets:
  N1: J1.pin_0, Teensy1.pin_31
  N2: J1.pin_1, R1.Pin_0, P1.Probe_tip, P1.Probe_meter_end
  N3: R1.Pin_1, Teensy1.pin_1, Teensy1.pin_32, P2.Probe_tip

notes:
  Form a voltage divider between FSR and a resistor. Then probe the signal using the Oscilloscope.

custom parts:
  Teensy 4.0: The Teensy is a complete USB-based microcontoller development system, in a very small footprint, capable of implementing many types of projects. All programming is done via the USB port. No special programmer is needed, only a standard micro-USB cable and a PC or Macintosh with a USB port.
