# Fritzing sketch 01.Button (saved by Fritzing 0.9.10b)
breadboards: 1

parts:
  Teensy1 = Teensy 4.0
  S1 = Pushbutton [package="[THT]"]
  LED1 = LED - 5mm [color="Red (633nm)" current=0.030 package="5 mm [THT]"]
  R1 = Resistor [tolerance=±5% power=0.25 resistance=10000 package=THT]
  R2 = Resistor [tolerance=±5% power=0.25 resistance=220 package=THT]

nets:
  N1: Teensy1.pin_1, Teensy1.pin_32, LED1.cathode, R1.Pin_0
  N2: Teensy1.pin_4, S1.Pin_1, S1.Pin_2, R1.Pin_1
  N3: Teensy1.pin_16, Teensy1.pin_31, S1.Pin_3, S1.Pin_4
  N4: Teensy1.pin_20, R2.Pin_0
  N5: LED1.anode, R2.Pin_1

notes:
  Resistor values are 220Ω for LED and 10KΩ for pull down. The LED pin is 13, and the button pin is 2.

custom parts:
  Teensy 4.0: The Teensy is a complete USB-based microcontoller development system, in a very small footprint, capable of implementing many types of projects. All programming is done via the USB port. No special programmer is needed, only a standard micro-USB cable and a PC or Macintosh with a USB port.
