# Fritzing sketch 02.AnalogInOutSerial (saved by Fritzing 0.9.10b)
breadboards: 1

parts:
  Teensy1 = Teensy 4.0
  R1 = Resistor [tolerance=±5% power=0.25 resistance=220 package=THT]
  LED1 = LED - 5mm [color="Red (633nm)" current=0.030 package="5 mm [THT]"]
  R2 = TRIMPOT [maximum_resistance=10kΩ knob_status=50% power=0.5W package=3386u]

nets:
  N1: Teensy1.pin_1, Teensy1.pin_32, LED1.anode, R2.CW
  N2: Teensy1.pin_11, R1.Pin_0
  N3: Teensy1.pin_21, R2.WIPER
  N4: Teensy1.pin_31, R2.CCW
  N5: R1.Pin_1, LED1.cathode

notes:
  The center pin of the potentiometer is connected to pin A0. Pin 9 is connected to LED via a 220Ω resistor.

custom parts:
  Teensy 4.0: The Teensy is a complete USB-based microcontoller development system, in a very small footprint, capable of implementing many types of projects. All programming is done via the USB port. No special programmer is needed, only a standard micro-USB cable and a PC or Macintosh with a USB port.
