# Fritzing sketch 01.LEDPWM (saved by Fritzing 0.9.10b)
circuit board: 8.46667cm x 5.64444cm
breadboards: 1

parts:
  Teensy1 = Teensy 4.0
  R1 = Resistor [tolerance=±5% power=0.25 resistance=220 package=THT]
  LED1 = LED - 5mm [color="Red (633nm)" current=0.030 package="5 mm [THT]"]

nets:
  N1: Teensy1.pin_1, Teensy1.pin_17, Teensy1.pin_32, LED1.anode
  N2: Teensy1.pin_11, R1.Pin_0
  N3: R1.Pin_1, LED1.cathode

notes:
  LED is connected to pin 9.

custom parts:
  Teensy 4.0: The Teensy is a complete USB-based microcontoller development system, in a very small footprint, capable of implementing many types of projects. All programming is done via the USB port. No special programmer is needed, only a standard micro-USB cable and a PC or Macintosh with a USB port.
