# Fritzing sketch 01.MIDISwitch (saved by Fritzing 0.9.10b)
breadboards: 1

parts:
  Teensy1 = Teensy 4.0
  S1 = Pushbutton [package="[THT]"]

nets:
  N1: Teensy1.pin_1, Teensy1.pin_17, Teensy1.pin_32, S1.Pin_1, S1.Pin_2
  N2: Teensy1.pin_4, S1.Pin_3, S1.Pin_4

notes:
  We will use Teensy's internal pull-up register for this exercise, so resistors are not required.

custom parts:
  Teensy 4.0: The Teensy is a complete USB-based microcontoller development system, in a very small footprint, capable of implementing many types of projects. All programming is done via the USB port. No special programmer is needed, only a standard micro-USB cable and a PC or Macintosh with a USB port.
