# Fritzing sketch 01.MIDIPot (saved by Fritzing 0.9.10b)
breadboards: 1

parts:
  Teensy1 = Teensy 4.0
  R2 = TRIMPOT [maximum_resistance=10kΩ knob_status=50% power=0.5W package=3386u]

nets (from the schematic view):
  N1: Teensy1.pin_1, Teensy1.pin_32
  N2: Teensy1.pin_21, R2.WIPER
  N3: Teensy1.pin_31, R2.CCW
  N4: Teensy1.pin33, R2.CW

custom parts:
  Teensy 4.0: The Teensy is a complete USB-based microcontoller development system, in a very small footprint, capable of implementing many types of projects. All programming is done via the USB port. No special programmer is needed, only a standard micro-USB cable and a PC or Macintosh with a USB port.
