# Fritzing sketch 01.MIDIAccelerometer (saved by Fritzing 0.9.10b)
breadboards: 1

parts:
  Teensy1 = Teensy 4.0
  Part1 = SparkFun_Tri_Axis_Accel_Breakout-LIS331  # not connected

nets:
  N1: Teensy1.pin_1, Teensy1.pin_32

custom parts:
  Teensy 4.0: The Teensy is a complete USB-based microcontoller development system, in a very small footprint, capable of implementing many types of projects. All programming is done via the USB port. No special programmer is needed, only a standard micro-USB cable and a PC or Macintosh with a USB port.
