# Fritzing sketch 02.SinewaveSynth (saved by Fritzing 0.9.10b)
breadboards: 1

parts:
  Teensy1 = Teensy 4.0
  R2 = TRIMPOT [maximum_resistance=10kΩ knob_status=50% power=0.5W package=3386u]
  S1 = Pushbutton [package="[THT]"]

nets (from the schematic view):
  N1: Teensy1.pin_1, Teensy1.pin_32
  N2: Teensy1.pin_21, S1.Pin_3, S1.Pin_4
  N3: Teensy1.pin_22, R2.WIPER
  N4: Teensy1.pin_31, R2.CCW
  N5: Teensy1.pin33, R2.CW, S1.Pin_1, S1.Pin_2

custom parts:
  Teensy 4.0: The Teensy is a complete USB-based microcontoller development system, in a very small footprint, capable of implementing many types of projects. All programming is done via the USB port. No special programmer is needed, only a standard micro-USB cable and a PC or Macintosh with a USB port.
